# Fritzing sketch car (saved by Fritzing 0.9.3b)
breadboards: 1

parts:
  Part1 = Arduino Uno (Rev3)
  HC-SR04_Sensor_1 = HC-SR04 Ultrasonic Distance Sensor [part_number=2]
  HC-SR04_Sensor_2 = HC-SR04 Ultrasonic Distance Sensor [part_number=1]
  HC-SR04_Sensor_3 = HC-SR04 Ultrasonic Distance Sensor [part_number=3]
  LED1 = LED - 5mm [color="Red (633nm)" package="5 mm [THT]"]

nets:
  N1: Part1.D8, LED1.anode
  N2: Part1.D2, HC-SR04_Sensor_1.TRIG
  N3: Part1.D3_PWM, HC-SR04_Sensor_1.ECHO
  N4: Part1.D4, HC-SR04_Sensor_2.TRIG
  N5: Part1.D5_PWM, HC-SR04_Sensor_2.ECHO
  N6: Part1.D6_PWM, HC-SR04_Sensor_3.TRIG
  N7: Part1.D7, HC-SR04_Sensor_3.ECHO
  VCC: Part1.5V, HC-SR04_Sensor_1.VCC, HC-SR04_Sensor_2.VCC, HC-SR04_Sensor_3.VCC, LED1.cathode
  GND: Part1.GND, HC-SR04_Sensor_1.GND, HC-SR04_Sensor_2.GND, HC-SR04_Sensor_3.GND
